# Fritzing sketch c01_display_prototype (saved by Fritzing 0.7.4b)
breadboards: 1

parts:
  MAX1 = MAX7219
  LED1 = LED - 5mm [color="Green (560nm)" package="5 mm [THT]"]
  LED4 = LED - 5mm [color="Green (560nm)" package="5 mm [THT]"]
  LED3 = LED - 5mm [color="Red (633nm)" package="5 mm [THT]"]
  LED2 = LED - 5mm [color="Yellow (595nm)" package="5 mm [THT]"]
  LED5 = LED - 5mm [color="Yellow (595nm)" package="5 mm [THT]"]
  LED11 = LED - 5mm [color="Yellow (595nm)" package="5 mm [THT]"]
  LED8 = LED - 5mm [color="Yellow (595nm)" package="5 mm [THT]"]
  LED6 = LED - 5mm [color="Red (633nm)" package="5 mm [THT]"]
  LED9 = LED - 5mm [color="Red (633nm)" package="5 mm [THT]"]
  LED12 = LED - 5mm [color="Red (633nm)" package="5 mm [THT]"]
  LED7 = LED - 5mm [color="Green (560nm)" package="5 mm [THT]"]
  LED10 = LED - 5mm [color="Green (560nm)" package="5 mm [THT]"]
  C1 = Electrolytic Capacitor [capacitance=10µF package="100 mil [THT, electrolytic]"]
  C2 = Ceramic Capacitor [capacitance=100nF package="100 mil [THT, multilayer]"]
  R1 = Resistor [tolerance=±5% resistance=68k package=THT]
  R2 = Resistor [tolerance=±5% resistance=47k package=THT]
  Arduino1 = Arduino

nets:
  N1: MAX1.Data_In, Arduino1.D5
  N2: MAX1.Digit_0, LED1.cathode, LED4.cathode, LED3.cathode, LED2.cathode, LED5.cathode, LED6.cathode
  N3: MAX1.Ground, C1.-, C2.1, Arduino1.GND
  N4: MAX1.Digit_1, LED11.cathode, LED8.cathode, LED9.cathode, LED12.cathode, LED7.cathode, LED10.cathode
  N5: MAX1.Chip_Select_(CS), Arduino1.D7
  N6: MAX1.Cock, Arduino1.D6
  N7: MAX1.Segment_A, LED1.anode, LED7.anode
  N8: MAX1.Segment_F, LED5.anode, LED11.anode
  N9: MAX1.Segment_B, LED2.anode, LED8.anode
  N10: MAX1.Segment_G, LED6.anode, LED12.anode
  N11: MAX1.Iset, R1.Pin_1, R2.Pin_1
  N12: MAX1.V+, C1.+, C2.0, R1.Pin_0, R2.Pin_0, Arduino1.+5V
  N13: MAX1.Segment_C, LED3.anode, LED9.anode
  N14: MAX1.Segment_E, LED4.anode, LED10.anode

custom parts:
  MAX7219: Serially Interfaced, 8-Digit, LED Display Drivers
